// Logisim project Cal.circ as structural Verilog: 9 circuits, main circuit main
module main (
  input  [3:0] Input_A,
  input  [3:0] Input_B,
  input  in_3,
  input  [2:0] in_4,
  input  [1:0] in_5,
  output [7:0] out_6
);

  calc calc_1 (.A(Input_A), .B(Input_B), .camp_selection(in_5), .Selection_Line(in_4), .Output(out_6), .out_6(in_3));

  // Notes on the sheet:
  //   0 0 - A Equal B
  //   0 1 - A Greter thenl B
  //   1 0 - A Less then B
  //   Calculator
  //   0 0 0 - Addition
  //   0 0 1 - Subtractor
  //   0 1 0 - Multiplier
  //   Magnitude Comparator
  //   0 1 1 - Unsigned Division ( Quotient )
  //   1 0 0 - Unsigned Division ( Reminder )
  //   Output
endmodule

module Adder (
  input  C_in,
  input  [3:0] A,
  input  [3:0] B,
  output [3:0] SUM,
  output Carry
);

  wire and_1_out, and_2_out, and_3_out, and_4_out, and_5_out, and_6_out, and_7_out, and_8_out, or_1_out,
       or_2_out, or_3_out, xor_1_out, xor_2_out, xor_3_out, xor_4_out;

  xor xor_1 (xor_1_out, A[0], B[0]);
  xor xor_2 (xor_2_out, A[1], B[1]);
  xor xor_3 (xor_3_out, A[2], B[2]);
  xor xor_4 (xor_4_out, A[3], B[3]);
  xor xor_5 (SUM[0], xor_1_out, C_in);
  and and_1 (and_1_out, xor_1_out, C_in);
  and and_2 (and_2_out, A[0], B[0]);
  and and_3 (and_3_out, xor_2_out, or_1_out);
  and and_4 (and_4_out, B[1], A[1]);
  and and_5 (and_5_out, xor_3_out, or_2_out);
  and and_6 (and_6_out, B[2], A[2]);
  buf and_7 (and_7_out, or_3_out);  // AND_Gate
  and and_8 (and_8_out, B[3], A[3]);
  xor xor_6 (SUM[1], xor_2_out, or_1_out);
  xor xor_7 (SUM[2], xor_3_out, or_2_out);
  xor xor_8 (SUM[3], xor_4_out, or_3_out);
  or or_1 (or_1_out, and_1_out, and_2_out);
  or or_2 (or_2_out, and_3_out, and_4_out);
  or or_3 (or_3_out, and_5_out, and_6_out);
  or or_4 (Carry, and_7_out, and_8_out);

  // Notes on the sheet:
  //   A - Input
  //   B - Input
endmodule

module Sub (
  input  C_in,
  input  [3:0] A,
  input  [3:0] B,
  output [3:0] SUM,
  output Carry
);

  wire and_1_out, and_2_out, and_3_out, and_4_out, and_5_out, and_6_out, and_7_out, and_8_out, not_1_out,
       not_2_out, not_3_out, not_4_out, not_5_out, not_6_out, not_7_out, not_8_out, or_1_out, or_2_out,
       or_3_out, xor_1_out, xor_2_out, xor_3_out, xor_4_out;

  not not_1 (not_1_out, A[2]);
  not not_2 (not_2_out, A[3]);
  xor xor_1 (xor_1_out, A[0], B[0]);
  not not_3 (not_3_out, A[0]);
  xor xor_2 (xor_2_out, A[1], B[1]);
  not not_4 (not_4_out, A[1]);
  xor xor_3 (xor_3_out, A[2], B[2]);
  xor xor_4 (xor_4_out, A[3], B[3]);
  xor xor_5 (SUM[0], xor_1_out, C_in);
  not not_5 (not_5_out, xor_1_out);
  and and_1 (and_1_out, not_5_out, C_in);
  and and_2 (and_2_out, not_3_out, B[0]);
  not not_6 (not_6_out, xor_2_out);
  and and_3 (and_3_out, not_6_out, or_1_out);
  and and_4 (and_4_out, B[1], not_4_out);
  not not_7 (not_7_out, xor_3_out);
  and and_5 (and_5_out, not_7_out, or_2_out);
  and and_6 (and_6_out, B[2], not_1_out);
  not not_8 (not_8_out, xor_4_out);
  and and_7 (and_7_out, not_8_out, or_3_out);
  and and_8 (and_8_out, B[3], not_2_out);
  xor xor_6 (SUM[1], xor_2_out, or_1_out);
  xor xor_7 (SUM[2], xor_3_out, or_2_out);
  xor xor_8 (SUM[3], xor_4_out, or_3_out);
  or or_1 (or_1_out, and_1_out, and_2_out);
  or or_2 (or_2_out, and_3_out, and_4_out);
  or or_3 (or_3_out, and_5_out, and_6_out);
  or or_4 (Carry, and_7_out, and_8_out);

  // Notes on the sheet:
  //   A - Input
  //   B - Input
endmodule

module multi (
  input  [3:0] X,
  input  [3:0] X_2,
  input  y0,
  input  y1,
  input  ZERO,
  input  [3:0] X_3,
  input  y2,
  input  [3:0] X_4,
  input  y3,
  output [7:0] \output 
);

  wire [2:0] and_15_out;
  wire [3:0] adder_2_carry, and_9_out, and_10_out, and_12_out;
  wire [3:1] adder_1_sum;
  wire [3:3] adder_1_carry;

  and and_1 (and_9_out[3], y1, X[3]);
  and and_2 (and_10_out[3], y2, X_3[3]);
  and and_3 (and_12_out[3], y3, X_4[3]);
  and and_4 (and_9_out[2], y1, X[2]);
  and and_5 (and_10_out[2], y2, X_3[2]);
  and and_6 (and_10_out[1], y2, X_3[1]);
  and and_7 (and_12_out[2], y3, X_4[2]);
  and and_8 (and_9_out[1], y1, X[1]);
  and and_9 (and_9_out[0], y1, X[0]);
  Adder adder_1 (
    .C_in(ZERO), .A(and_9_out), .B({ZERO, and_15_out}), .SUM({adder_1_sum, \output [1]}),
    .Carry(adder_1_carry[3]));
  and and_10 (and_10_out[0], y2, X_3[0]);
  and and_11 (and_12_out[1], y3, X_4[1]);
  and and_12 (and_12_out[0], y3, X_4[0]);
  Adder adder_2 (
    .C_in(ZERO), .A(and_10_out), .B({adder_1_carry[3], adder_1_sum}),
    .SUM({adder_2_carry[2:0], \output [2]}), .Carry(adder_2_carry[3]));
  Adder adder_3 (.C_in(ZERO), .A(and_12_out), .B(adder_2_carry), .SUM(\output [6:3]), .Carry(\output [7]));
  and and_13 (and_15_out[2], y0, X_2[3]);
  and and_14 (and_15_out[1], y0, X_2[2]);
  and and_15 (and_15_out[0], y0, X_2[1]);
  and and_16 (\output [0], y0, X_2[0]);
endmodule

module adder_div (
  input  C1,
  input  R,
  input  B,
  output CO,
  output D
);

  wire and_1_out, and_2_out, and_3_out, xor_1_out;

  and and_1 (and_1_out, R, B);
  and and_2 (and_2_out, R, C1);
  and and_3 (and_3_out, B, C1);
  xor xor_1 (xor_1_out, R, B);
  or or_1 (CO, and_1_out, and_2_out, and_3_out);
  xor xor_2 (D, C1, xor_1_out);
endmodule

module Cell (
  input  C1,
  input  R,
  input  nB,
  input  N,
  output CO,
  output D,
  output R_prime,
  output B
);

  adder_div adder_div_1 (.C1(C1), .R(R), .B(nB), .CO(CO), .D(D));
  Multiplexer multiplexer_1 (.in0(D), .in1(R), .out(R_prime), .sel(N));  // open: en

  assign B = nB;
endmodule

module DIV (
  input  [3:0] A,
  input  [3:0] B,
  output [3:0] Q,
  output [3:0] R
);

  wire cell_1_b, cell_1_d, cell_2_b, cell_2_d, cell_3_b, cell_3_d, cell_4_d, cell_5_b, cell_5_co,
       cell_5_r_prime, cell_6_b, cell_6_co, cell_6_r_prime, cell_7_b, cell_7_co, cell_7_r_prime, cell_8_co,
       cell_9_b, cell_9_co, cell_9_r_prime, cell_10_b, cell_10_co, cell_10_r_prime, cell_11_b, cell_11_co,
       cell_11_r_prime, cell_12_co, cell_13_b, cell_13_co, cell_13_r_prime, cell_14_b, cell_14_co,
       cell_14_r_prime, cell_15_b, cell_15_co, cell_15_r_prime, cell_16_co, not_5_out, not_6_out, not_7_out,
       not_8_out;

  not not_1 (Q[3], cell_1_d);
  not not_2 (Q[2], cell_2_d);
  not not_3 (Q[1], cell_3_d);
  not not_4 (Q[0], cell_4_d);
  not not_5 (not_5_out, B[0]);
  not not_6 (not_6_out, B[1]);
  not not_7 (not_7_out, B[2]);
  not not_8 (not_8_out, B[3]);
  Cell cell_1 (
    .C1(cell_5_co), .R(1'b0), .nB(not_8_out), .N(cell_1_d), .B(cell_1_b), .D(cell_1_d));  // open: CO, R_prime
  Cell cell_2 (
    .C1(cell_6_co), .R(cell_5_r_prime), .nB(cell_1_b), .N(cell_2_d), .B(cell_2_b), .D(cell_2_d));  // open: CO, R_prime
  Cell cell_3 (
    .C1(cell_7_co), .R(cell_6_r_prime), .nB(cell_2_b), .N(cell_3_d), .B(cell_3_b), .D(cell_3_d));  // open: CO, R_prime
  Cell cell_4 (
    .C1(cell_8_co), .R(cell_7_r_prime), .nB(cell_3_b), .N(cell_4_d), .D(cell_4_d), .R_prime(R[3]));  // open: B, CO
  Cell cell_5 (
    .C1(cell_9_co), .R(1'b0), .nB(not_7_out), .N(cell_1_d), .B(cell_5_b), .CO(cell_5_co),
    .R_prime(cell_5_r_prime));  // open: D
  Cell cell_6 (
    .C1(cell_10_co), .R(cell_9_r_prime), .nB(cell_5_b), .N(cell_2_d), .B(cell_6_b), .CO(cell_6_co),
    .R_prime(cell_6_r_prime));  // open: D
  Cell cell_7 (
    .C1(cell_11_co), .R(cell_10_r_prime), .nB(cell_6_b), .N(cell_3_d), .B(cell_7_b), .CO(cell_7_co),
    .R_prime(cell_7_r_prime));  // open: D
  Cell cell_8 (
    .C1(cell_12_co), .R(cell_11_r_prime), .nB(cell_7_b), .N(cell_4_d), .CO(cell_8_co), .R_prime(R[2]));  // open: B, D
  Cell cell_9 (
    .C1(cell_13_co), .R(1'b0), .nB(not_6_out), .N(cell_1_d), .B(cell_9_b), .CO(cell_9_co),
    .R_prime(cell_9_r_prime));  // open: D
  Cell cell_10 (
    .C1(cell_14_co), .R(cell_13_r_prime), .nB(cell_9_b), .N(cell_2_d), .B(cell_10_b), .CO(cell_10_co),
    .R_prime(cell_10_r_prime));  // open: D
  Cell cell_11 (
    .C1(cell_15_co), .R(cell_14_r_prime), .nB(cell_10_b), .N(cell_3_d), .B(cell_11_b), .CO(cell_11_co),
    .R_prime(cell_11_r_prime));  // open: D
  Cell cell_12 (
    .C1(cell_16_co), .R(cell_15_r_prime), .nB(cell_11_b), .N(cell_4_d), .CO(cell_12_co), .R_prime(R[1]));  // open: B, D
  Cell cell_13 (
    .C1(1'b1), .R(A[3]), .nB(not_5_out), .N(cell_1_d), .B(cell_13_b), .CO(cell_13_co),
    .R_prime(cell_13_r_prime));  // open: D
  Cell cell_14 (
    .C1(1'b1), .R(A[2]), .nB(cell_13_b), .N(cell_2_d), .B(cell_14_b), .CO(cell_14_co),
    .R_prime(cell_14_r_prime));  // open: D
  Cell cell_15 (
    .C1(1'b1), .R(A[1]), .nB(cell_14_b), .N(cell_3_d), .B(cell_15_b), .CO(cell_15_co),
    .R_prime(cell_15_r_prime));  // open: D
  Cell cell_16 (.C1(1'b1), .R(A[0]), .nB(cell_15_b), .N(cell_4_d), .CO(cell_16_co), .R_prime(R[0]));  // open: B, D
endmodule

module calc (
  input  [3:0] A,
  input  [3:0] B,
  input  [2:0] Selection_Line,
  input  [1:0] camp_selection,
  output [7:0] Output,
  output out_6
);

  wire comp_1_equal, comp_1_greter_then, comp_1_less_then;
  wire [3:0] Adder_sum, Divider_q, Divider_r, Sub_sum;
  wire [7:0] bit_extender_1_out, bit_extender_2_out, bit_extender_3_out, bit_extender_4_out,
       Multiplier_output;

  multi Multiplier (
    .y0(B[0]), .y1(B[1]), .y2(B[2]), .y3(B[3]), .\output (Multiplier_output), .ZERO(1'b0), .X(A), .X_3(A),
    .X_4(A), .X_2(A));
  DIV Divider (.A(A), .B(B), .Q(Divider_q), .R(Divider_r));
  Adder Adder (.C_in(1'b0), .A(A), .B(B), .SUM(Adder_sum));  // open: Carry
  Sub Sub (.C_in(1'b0), .A(A), .B(B), .SUM(Sub_sum));  // open: Carry
  assign bit_extender_1_out = {{4{1'b0}}, Divider_q};  // Bit_Extender bit_extender_1
  assign bit_extender_2_out = {{4{1'b0}}, Divider_r};  // Bit_Extender bit_extender_2
  assign bit_extender_3_out = {{4{1'b0}}, Adder_sum};  // Bit_Extender bit_extender_3
  assign bit_extender_4_out = {{4{1'b0}}, Sub_sum};  // Bit_Extender bit_extender_4
  Multiplexer #(.select(3), .width(8)) multiplexer_1 (
    .in0(bit_extender_3_out), .in1(bit_extender_4_out), .in2(Multiplier_output), .in3(bit_extender_1_out),
    .in4(bit_extender_2_out), .out(Output), .sel(Selection_Line));  // open: in5, in6, in7, en
  comp comp_1 (.A(A), .B(B), .Equal(comp_1_equal), .Greter_then(comp_1_greter_then), .Less_then(comp_1_less_then));
  Multiplexer #(.select(2)) multiplexer_2 (
    .in0(comp_1_equal), .in1(comp_1_greter_then), .in2(comp_1_less_then), .out(out_6), .sel(camp_selection));  // open: in3, en
endmodule

module comp (
  input  [3:0] A,
  input  [3:0] B,
  output Equal,
  output Greter_then,
  output Less_then
);

  wire and_1_out, and_2_out, and_3_out, and_4_out, and_5_out, and_6_out, and_7_out, and_8_out, not_1_out,
       not_2_out, not_3_out, not_4_out, not_5_out, not_6_out, not_7_out, not_8_out, xnor_1_out, xnor_2_out,
       xnor_3_out, xnor_4_out;

  not not_1 (not_1_out, B[0]);
  not not_2 (not_2_out, B[1]);
  not not_3 (not_3_out, B[2]);
  not not_4 (not_4_out, B[3]);
  not not_5 (not_5_out, A[0]);
  not not_6 (not_6_out, A[1]);
  not not_7 (not_7_out, A[2]);
  not not_8 (not_8_out, A[3]);
  xnor xnor_1 (xnor_1_out, B[0], A[0]);
  xnor xnor_2 (xnor_2_out, B[1], A[1]);
  xnor xnor_3 (xnor_3_out, B[2], A[2]);
  xnor xnor_4 (xnor_4_out, B[3], A[3]);
  and and_1 (and_1_out, not_1_out, A[0]);
  and and_2 (and_2_out, not_2_out, A[1]);
  and and_3 (and_3_out, not_3_out, A[2]);
  and and_4 (and_4_out, not_4_out, A[3]);
  and and_5 (and_5_out, not_5_out, B[0]);
  and and_6 (and_6_out, not_6_out, B[1]);
  and and_7 (and_7_out, not_7_out, B[2]);
  and and_8 (and_8_out, not_8_out, B[3]);
  and and_9 (Equal, xnor_1_out, xnor_2_out, xnor_3_out, xnor_4_out);
  or or_1 (Greter_then, and_1_out, and_2_out, and_3_out, and_4_out);
  or or_2 (Less_then, and_5_out, and_6_out, and_7_out, and_8_out);
endmodule
